// Digital circuit DataController.dig as structural Verilog
module DataController (
  input  [31:0] AddressIn,
  input  AddressWe,
  input  Clock,
  input  DataOe,
  input  [31:0] DinMMU,
  input  Signed,
  input  half,
  input  \byte ,
  output [31:0] AddressOut,
  output [31:0] DoCPU,
  output [3:0] ByteSelect
);

  wire and_1_out, and_2_out, and_3_out, decoder_1_out_1, decoder_1_out_2, decoder_1_out_3, or_1_out;
  wire [1:0] not_2_out;
  wire [3:0] decoder_1_out_0;
  wire [31:0] bitextender_1_out, bitextender_2_out, bitextender_3_out, bitextender_4_out, bitextender_5_out,
       bitextender_6_out, bitextender_7_out, multiplexer_1_out, multiplexer_2_out;

  Register #(.Bits(32)) register_1 (.D(AddressIn), .C(Clock), .en(AddressWe), .Q(AddressOut));
  BitExtender #(.outputBits(32)) bitextender_1 (.in(DinMMU[7:0]), .out(bitextender_1_out));
  BitExtender #(.inputBits(16), .outputBits(32)) bitextender_2 (.in(DinMMU[15:0]), .out(bitextender_2_out));
  BitExtender #(.outputBits(32)) bitextender_3 (.in(DinMMU[15:8]), .out(bitextender_3_out));
  BitExtender #(.inputBits(16), .outputBits(32)) bitextender_4 (.in(DinMMU[23:8]), .out(bitextender_4_out));
  BitExtender #(.outputBits(32)) bitextender_5 (.in(DinMMU[23:16]), .out(bitextender_5_out));
  BitExtender #(.inputBits(16), .outputBits(32)) bitextender_6 (.in(DinMMU[31:16]), .out(bitextender_6_out));
  BitExtender #(.outputBits(32)) bitextender_7 (.in(DinMMU[31:24]), .out(bitextender_7_out));
  not not_1 (not_2_out[0], Signed);
  not not_2 (not_2_out[1], \byte );
  Multiplexer #(.Selector_Bits(4), .Bits(32)) multiplexer_1 (
    .sel({AddressOut[1:0], not_2_out}), .in_0(bitextender_1_out), .in_1({{24{1'b0}}, DinMMU[7:0]}),
    .in_2(bitextender_2_out), .in_3({{16{1'b0}}, DinMMU[15:0]}), .in_4(bitextender_3_out),
    .in_5({{24{1'b0}}, DinMMU[15:8]}), .in_6(bitextender_4_out), .in_7({{16{1'b0}}, DinMMU[23:8]}),
    .in_8(bitextender_5_out), .in_9({{24{1'b0}}, DinMMU[23:16]}), .in_10(bitextender_6_out),
    .in_11({{16{1'b0}}, DinMMU[31:16]}), .in_12(bitextender_7_out), .in_13({{24{1'b0}}, DinMMU[31:24]}),
    .in_14({32{1'b0}}), .in_15({32{1'b0}}), .out(multiplexer_1_out));
  Decoder #(.Selector_Bits(2)) decoder_1 (
    .sel(AddressOut[1:0]), .out_0(decoder_1_out_0[0]), .out_1(decoder_1_out_1), .out_2(decoder_1_out_2),
    .out_3(decoder_1_out_3));
  Multiplexer #(.Bits(32)) multiplexer_2 (
    .sel(or_1_out), .in_0(DinMMU), .in_1(multiplexer_1_out), .out(multiplexer_2_out));
  or or_1 (or_1_out, half, \byte );
  assign DoCPU = DataOe ? multiplexer_2_out : 32'bz;  // Driver driver_1
  and and_1 (and_1_out, decoder_1_out_0[0], half);
  and and_2 (and_2_out, decoder_1_out_1, half);
  and and_3 (and_3_out, decoder_1_out_2, half);
  or or_2 (decoder_1_out_0[1], and_1_out, decoder_1_out_1);
  or or_3 (decoder_1_out_0[2], and_2_out, decoder_1_out_2);
  or or_4 (decoder_1_out_0[3], and_3_out, decoder_1_out_3);
  Multiplexer #(.Bits(4)) multiplexer_3 (.sel(or_1_out), .in_0(4'b1111), .in_1(decoder_1_out_0), .out(ByteSelect));
endmodule
