// Digital circuit IO.dig as structural Verilog
module IO (
  input  [31:0] Add,
  input  [31:0] Din,
  input  We,
  input  Clock,
  input  Re,
  output [31:0] O
);

  wire and_1_out, and_2_out, and_3_out, and_4_out;
  wire [0:0] keyboard_1_av;
  wire [4:0] ioaddressmap_1_en;
  wire [15:0] keyboard_1_d;
  wire [31:0] register_1_q;

  IOAddressMap ioaddressmap_1 (.Addr(Add), .en(ioaddressmap_1_en));
  and and_1 (and_1_out, We, ioaddressmap_1_en[0]);
  and and_2 (and_2_out, We, ioaddressmap_1_en[1]);
  and and_3 (and_3_out, We, ioaddressmap_1_en[2]);
  and and_4 (and_4_out, Re, ioaddressmap_1_en[3]);
  Terminal terminal_1 (.D(Din), .C(Clock), .en(and_1_out));
  GraphicCard #(.Bits(16)) graphiccard_1 (
    .A(Add[16:2]), .str(and_2_out), .C(Clock), .ld(1'b0), .B(register_1_q[0]), .D(Din[15:0]));
  Register #(.Bits(32)) register_1 (.D(Din), .C(Clock), .en(and_3_out), .Q(register_1_q));
  Keyboard keyboard_1 (.C(Clock), .en(and_4_out), .D(keyboard_1_d), .av(keyboard_1_av[0]));
  Multiplexer #(.Bits(32)) multiplexer_1 (
    .sel(ioaddressmap_1_en[4]), .in_0({{16{1'b0}}, keyboard_1_d}), .in_1({{31{1'b0}}, keyboard_1_av[0]}),
    .out(O));
endmodule
