// Digital circuit IOAddressMap.dig as structural Verilog
module IOAddressMap (
  input  [31:0] Addr,
  output [4:0] en
);

  nor nor_1 (en[0], ~Addr[2], Addr[3], Addr[4], Addr[5], Addr[6], Addr[7], Addr[8], Addr[9], Addr[10], Addr[11], Addr[12], Addr[13], Addr[14], Addr[15], Addr[16], ~Addr[17], Addr[18], ~Addr[19], Addr[20], Addr[21], Addr[22], Addr[23], Addr[24], Addr[25], Addr[26], Addr[27], Addr[28], Addr[29], Addr[30], Addr[31]);  // NOr
  nor nor_2 (en[1], Addr[17], Addr[18], ~Addr[19], Addr[20], Addr[21], Addr[22], Addr[23], Addr[24], Addr[25], Addr[26], Addr[27], Addr[28], Addr[29], Addr[30], Addr[31]);  // NOr
  nor nor_3 (en[2], Addr[2], Addr[3], Addr[4], Addr[5], Addr[6], Addr[7], Addr[8], Addr[9], Addr[10], Addr[11], Addr[12], Addr[13], Addr[14], Addr[15], Addr[16], ~Addr[17], Addr[18], ~Addr[19], Addr[20], Addr[21], Addr[22], Addr[23], Addr[24], Addr[25], Addr[26], Addr[27], Addr[28], Addr[29], Addr[30], Addr[31]);  // NOr
  nor nor_4 (en[3], Addr[2], Addr[3], Addr[4], ~Addr[5], Addr[6], Addr[7], Addr[8], Addr[9], Addr[10], Addr[11], Addr[12], Addr[13], Addr[14], Addr[15], Addr[16], ~Addr[17], Addr[18], ~Addr[19], Addr[20], Addr[21], Addr[22], Addr[23], Addr[24], Addr[25], Addr[26], Addr[27], Addr[28], Addr[29], Addr[30], Addr[31]);  // NOr
  nor nor_5 (en[4], ~Addr[2], Addr[3], Addr[4], ~Addr[5], Addr[6], Addr[7], Addr[8], Addr[9], Addr[10], Addr[11], Addr[12], Addr[13], Addr[14], Addr[15], Addr[16], ~Addr[17], Addr[18], ~Addr[19], Addr[20], Addr[21], Addr[22], Addr[23], Addr[24], Addr[25], Addr[26], Addr[27], Addr[28], Addr[29], Addr[30], Addr[31]);  // NOr

  // Notes on the sheet:
  //   Terminal:
  //   0x 00 0A 00 04
  //   0x 00 0A 00 07
  //   GrRAM:
  //   0x 00 08 00 00
  //   0x 00 08 FF FF
  //   GrRAM Page:
  //   0x 00 0A 00 00
  //   0x 00 0A 00 03
  //   Keyboard data:
  //   0x 00 0A 00 20
  //   0x 00 0A 00 23
  //   Keyboard Status:
  //   0x 00 0A 00 24
  //   0x 00 0A 00 27
endmodule
