// Digital circuit InstructionSplicer.dig as structural Verilog
module InstructionSplicer (
  input  [2:0] ImmSel,
  input  [31:0] INSin,
  output [6:0] funct7,
  output [2:0] funct3,
  output [6:0] opcode,
  output [4:0] rs1,
  output [4:0] rs2,
  output [4:0] rd,
  output [31:0] Imm
);

  wire [31:0] bitextender_1_out, bitextender_2_out, bitextender_3_out, bitextender_4_out;

  BitExtender #(.inputBits(12), .outputBits(32)) bitextender_1 (.in(INSin[31:20]), .out(bitextender_1_out));
  BitExtender #(.inputBits(12), .outputBits(32)) bitextender_2 (
    .in({INSin[31:25], INSin[11:7]}), .out(bitextender_2_out));
  BitExtender #(.inputBits(13), .outputBits(32)) bitextender_3 (
    .in({INSin[31], INSin[7], INSin[30:25], INSin[11:8], 1'b0}), .out(bitextender_3_out));
  BitExtender #(.inputBits(21), .outputBits(32)) bitextender_4 (
    .in({INSin[31], INSin[19:12], INSin[20], INSin[30:21], 1'b0}), .out(bitextender_4_out));
  Multiplexer #(.Selector_Bits(3), .Bits(32)) multiplexer_1 (
    .sel(ImmSel), .in_0(bitextender_1_out), .in_1(bitextender_2_out), .in_2(bitextender_3_out),
    .in_3({INSin[31:12], {12{1'b0}}}), .in_4(bitextender_4_out), .in_5({32{1'b0}}), .in_6({32{1'b0}}),
    .in_7({32{1'b0}}), .out(Imm));

  assign funct3 = INSin[14:12];
  assign funct7 = INSin[31:25];
  assign opcode = INSin[6:0];
  assign rd = INSin[11:7];
  assign rs1 = INSin[19:15];
  assign rs2 = INSin[24:20];

  // Notes on the sheet:
  //   ImmSel: 000: I
  //   001: S
  //   010: B
  //   011: U
  //   100: J
  //   I
  //   S
  //   B
  //   U
  //   J
endmodule
