// Digital circuit MMU.dig as structural Verilog
module MMU (
  input  [31:0] Din,
  input  We,
  input  Clock,
  input  [31:0] AddressIn,
  input  [3:0] ByteSelect,
  output [31:0] Dout
);

  wire [3:0] and_1_out, bitextender_1_out;

  BitExtender #(.inputBits(1), .outputBits(4)) bitextender_1 (.in(We), .out(bitextender_1_out));
  assign and_1_out = bitextender_1_out & ByteSelect;  // And and_1, 4 bits wide
  RAMDualPort #(.AddrBits(16), .Bits(8)) Byte_0 (
    .A(AddressIn[17:2]), .Din(Din[7:0]), .str(and_1_out[0]), .C(Clock), .ld(1'b1), .D(Dout[7:0]));
  RAMDualPort #(.AddrBits(16), .Bits(8)) Byte_1 (
    .A(AddressIn[17:2]), .Din(Din[15:8]), .str(and_1_out[1]), .C(Clock), .ld(1'b1), .D(Dout[15:8]));
  RAMDualPort #(.AddrBits(16), .Bits(8)) Byte_2 (
    .A(AddressIn[17:2]), .Din(Din[23:16]), .str(and_1_out[2]), .C(Clock), .ld(1'b1), .D(Dout[23:16]));
  RAMDualPort #(.AddrBits(16), .Bits(8)) Byte_3 (
    .A(AddressIn[17:2]), .Din(Din[31:24]), .str(and_1_out[3]), .C(Clock), .ld(1'b1), .D(Dout[31:24]));
endmodule
