// Digital circuit MemoryMapper.dig as structural Verilog
module MemoryMapper (
  input  Clock,
  input  [31:0] Din,
  input  [31:0] Ain,
  input  [31:0] INSAin,
  input  [3:0] ByteSelect,
  input  We,
  input  [2:0] RegInsel,
  output [31:0] INSout,
  output [31:0] Dout
);

  wire and_1_out, and_2_out, decoder_1_out_1;
  wire [2:0] addressspace_1_enable, addressspace_2_enable;
  wire [31:0] io_1_p6, multiplexer_2_out, ram_256kb_1_dout, ram_256kb_1_insout, romdualport_1_d1,
       romdualport_1_d2;

  AddressSpace addressspace_1 (.Ain(Ain), .Enable(addressspace_1_enable));
  AddressSpace addressspace_2 (.Ain(INSAin), .Enable(addressspace_2_enable));
  and and_1 (and_1_out, We, addressspace_1_enable[1]);
  and and_2 (and_2_out, We, addressspace_1_enable[2]);
  Decoder #(.Selector_Bits(3)) decoder_1 (
    .sel(RegInsel), .out_1(decoder_1_out_1));  // open: out_0, out_2, out_3, out_4, out_5, out_6, out_7
  ROMDualPort #(.AddrBits(16), .isProgramMemory("true"), .Bits(32)) romdualport_1 (
    .A1(Ain[17:2]), .s1(1'b1), .A2(INSAin[17:2]), .s2(1'b1), .D1(romdualport_1_d1), .D2(romdualport_1_d2));
  RAM_256KB ram_256kb_1 (
    .INSAddressIn(INSAin[17:2]), .ByteSelect(ByteSelect), .AddressIn(Ain[17:2]), .Din(Din), .We(and_1_out),
    .Clock(Clock), .Dout(ram_256kb_1_dout), .INSout(ram_256kb_1_insout));
  // IO io_1: pin names not known; wires that end beside it: Ain, Din, and_2_out, Clock, decoder_1_out_1, io_1_p6
  Multiplexer #(.Bits(32)) multiplexer_1 (
    .sel(addressspace_2_enable[1]), .in_0(romdualport_1_d2), .in_1(ram_256kb_1_insout), .out(INSout));
  Multiplexer #(.Bits(32)) multiplexer_2 (
    .sel(addressspace_1_enable[1]), .in_0(romdualport_1_d1), .in_1(ram_256kb_1_dout), .out(multiplexer_2_out));
  Multiplexer #(.Bits(32)) multiplexer_3 (
    .sel(addressspace_1_enable[2]), .in_0(multiplexer_2_out), .in_1(io_1_p6), .out(Dout));

  // Notes on the sheet:
  //   romdualport_1 loads rom.intel.hex
endmodule
