// Digital circuit PcInSelector.dig as structural Verilog
module PcInSelector (
  input  [1:0] BranchIns,
  input  [1:0] PcInSel,
  input  [1:0] Flags,
  input  [31:0] ALU,
  input  [31:0] AdAdd,
  input  [31:0] PC_plus_4,
  output [31:0] PC
);

  wire multiplexer_2_out, not_1_out, not_2_out;
  wire [31:0] multiplexer_1_out;

  not not_1 (not_1_out, Flags[1]);
  not not_2 (not_2_out, Flags[0]);
  Multiplexer #(.Bits(32)) multiplexer_1 (
    .sel(multiplexer_2_out), .in_0(PC_plus_4), .in_1(AdAdd), .out(multiplexer_1_out));
  Multiplexer #(.Selector_Bits(2)) multiplexer_2 (
    .sel(BranchIns), .in_0(Flags[1]), .in_1(not_1_out), .in_2(Flags[0]), .in_3(not_2_out),
    .out(multiplexer_2_out));
  Multiplexer #(.Selector_Bits(2), .Bits(32)) multiplexer_3 (
    .sel(PcInSel), .in_0(PC_plus_4), .in_1(AdAdd), .in_2(ALU), .in_3(multiplexer_1_out), .out(PC));

  // Notes on the sheet:
  //   BranchIns: 00: BEQ
  //   01: BNE
  //   10: BLT
  //   11: BGE
  //   Flags: Z,LessThan
endmodule
