// Digital circuit Program Counter.dig as structural Verilog
module Program_Counter (
  input  [31:0] Din,
  input  Clock,
  input  We,
  input  Oe,
  input  Inc,
  output [31:0] Dout
);

  wire or_1_out;
  wire [31:0] add_1_s, multiplexer_1_out, register_1_q;

  or or_1 (or_1_out, We, Inc);
  Multiplexer #(.Bits(32)) multiplexer_1 (.sel(Inc), .in_0(Din), .in_1(add_1_s), .out(multiplexer_1_out));
  Register #(.Bits(32), .isProgramCounter("true")) register_1 (
    .D(multiplexer_1_out), .C(Clock), .en(or_1_out), .Q(register_1_q));
  Add #(.Bits(32)) add_1 (.a(32'h4), .b(register_1_q), .c_i(1'b0), .s(add_1_s));  // open: c_o
  assign Dout = Oe ? register_1_q : 32'bz;  // Driver driver_1

  // Notes on the sheet:
  //   Inc: Increase by 4 (4 bytes = 32 bits)
endmodule
