// Digital circuit ProgramCounter.dig as structural Verilog
module ProgramCounter (
  input  Clock,
  input  [31:0] Din,
  output [31:0] Dout,
  output [31:0] PC_plus_4
);

  Register #(.Bits(32), .isProgramCounter("true")) register_1 (.D({Din[31:1], 1'b0}), .C(Clock), .en(1'b1), .Q(Dout));
  Add #(.Bits(32)) add_1 (.a(Dout), .b(32'h4), .c_i(1'b0), .s(PC_plus_4));  // open: c_o
endmodule
