// Digital circuit Registers.dig as structural Verilog
module Registers (
  input  [31:0] Din,
  input  Clock,
  input  [4:0] Address1,
  input  [4:0] Address2,
  input  We1,
  input  We2,
  input  Oe1,
  input  Oe2,
  output [31:0] Dout
);

  wire and_1_out, and_2_out, and_3_out, and_4_out, or_1_out, or_2_out;
  wire [4:0] multiplexer_1_out;
  wire [31:0] and_5_out, and_6_out, bitextender_1_out, bitextender_2_out, multiplexer_2_out,
       Registers_1_31_da, Registers_1_31_db;

  or or_1 (or_1_out, We1, We2);
  Multiplexer #(.Bits(5)) multiplexer_1 (.sel(We1), .in_0(Address2), .in_1(Address1), .out(multiplexer_1_out));
  RegisterFile #(.AddrBits(5), .Bits(32)) Registers_1_31 (
    .Din(Din), .we(or_1_out), .Rw(multiplexer_1_out), .C(Clock), .Ra(Address1), .Rb(Address2),
    .Da(Registers_1_31_da), .Db(Registers_1_31_db));
  and and_1 (and_1_out, ~Address1[0], ~Address1[1], ~Address1[2], ~Address1[3], ~Address1[4]);  // And
  and and_2 (and_2_out, ~Address2[0], ~Address2[1], ~Address2[2], ~Address2[3], ~Address2[4]);  // And
  and and_3 (and_3_out, and_1_out, Oe1);
  BitExtender #(.inputBits(1), .outputBits(32)) bitextender_1 (.in(and_3_out), .out(bitextender_1_out));
  and and_4 (and_4_out, and_2_out, Oe2);
  BitExtender #(.inputBits(1), .outputBits(32)) bitextender_2 (.in(and_4_out), .out(bitextender_2_out));
  assign and_5_out = Registers_1_31_da & ~bitextender_1_out;  // And and_5, 32 bits wide
  assign and_6_out = Registers_1_31_db & ~bitextender_2_out;  // And and_6, 32 bits wide
  or or_2 (or_2_out, Oe1, Oe2);
  Multiplexer #(.Bits(32)) multiplexer_2 (.sel(Oe2), .in_0(and_5_out), .in_1(and_6_out), .out(multiplexer_2_out));
  assign Dout = or_2_out ? multiplexer_2_out : 32'bz;  // Driver driver_1
endmodule
