// Digital circuit SLL.dig as structural Verilog
module SLL (
  input  [31:0] in,
  input  [4:0] shift,
  output [31:0] out
);

  wire [31:0] multiplexer_1_out, multiplexer_2_out, multiplexer_3_out, multiplexer_4_out;

  Multiplexer #(.Bits(32)) multiplexer_1 (.sel(shift[0]), .in_0(in), .in_1({in[30:0], 1'b0}), .out(multiplexer_1_out));
  Multiplexer #(.Bits(32)) multiplexer_2 (
    .sel(shift[1]), .in_0(multiplexer_1_out), .in_1({multiplexer_1_out[29:0], 2'b00}), .out(multiplexer_2_out));
  Multiplexer #(.Bits(32)) multiplexer_3 (
    .sel(shift[2]), .in_0(multiplexer_2_out), .in_1({multiplexer_2_out[27:0], 4'b0000}),
    .out(multiplexer_3_out));
  Multiplexer #(.Bits(32)) multiplexer_4 (
    .sel(shift[3]), .in_0(multiplexer_3_out), .in_1({multiplexer_3_out[23:0], {8{1'b0}}}),
    .out(multiplexer_4_out));
  Multiplexer #(.Bits(32)) multiplexer_5 (
    .sel(shift[4]), .in_0(multiplexer_4_out), .in_1({multiplexer_4_out[15:0], {16{1'b0}}}), .out(out));
endmodule
