// Digital circuit ALU.dig as structural Verilog
module ALU (
  input  [4:0] OPSELECT,
  input  [31:0] B,
  input  [31:0] A,
  output [31:0] O,
  output [1:0] Flags
);

  wire Adder_c_o, and_1_out, and_2_out, and_3_out, and_4_out, and_6_out, decoder_1_out_1, decoder_1_out_5,
       decoder_1_out_6, decoder_1_out_11, decoder_1_out_13, decoder_1_out_14, decoder_1_out_16,
       decoder_1_out_17, or_3_out, or_4_out, or_5_out;
  wire [0:0] not_2_out, xor_1_out;
  wire [31:0] Adder_s, and_5_out, mul_1_mul, multiplexer_1_out, multiplexer_2_out, multiplexer_3_out,
       not_1_out, or_6_out, sll_1_out, sra_1_out, srl_1_out, sub_1_s, sub_2_s, xor_2_out;
  wire [31:1] multiplexer_4_out;
  wire [63:32] mul_1_mul_2;

  Decoder #(.Selector_Bits(5)) decoder_1 (
    .sel(OPSELECT), .out_1(decoder_1_out_1), .out_5(decoder_1_out_5), .out_6(decoder_1_out_6),
    .out_11(decoder_1_out_11), .out_13(decoder_1_out_13), .out_14(decoder_1_out_14),
    .out_16(decoder_1_out_16), .out_17(decoder_1_out_17));  // open: out_0, out_2, out_3, out_4, out_7, out_8, out_9, out_10, out_12, out_15, out_18, out_19, out_20, out_21, out_22, out_23, out_24, out_25, out_26, out_27, out_28, out_29, out_30, out_31
  // Or or_1 has open pins: In_1=decoder_1_out_16, In_2=decoder_1_out_17, out=open
  // Or or_2 has open pins: In_1=decoder_1_out_14, In_2=decoder_1_out_16, out=open
  or or_3 (or_3_out, decoder_1_out_11, decoder_1_out_13);
  and and_1 (and_1_out, A[31], or_3_out);
  and and_2 (and_2_out, multiplexer_1_out[31], decoder_1_out_11);
  assign not_1_out = ~B;  // Not not_1, 32 bits wide
  or or_4 (or_4_out, decoder_1_out_1, decoder_1_out_5, decoder_1_out_6);
  and and_3 (and_3_out, ~A[31], B[31], Adder_s[31]);  // And
  Multiplexer #(.Bits(32)) multiplexer_1 (.sel(or_4_out), .in_0(B), .in_1(not_1_out), .out(multiplexer_1_out));
  Mul #(.Bits(32)) mul_1 (.a(A), .b(multiplexer_1_out), .mul({mul_1_mul_2, mul_1_mul}));
  or or_5 (or_5_out, and_3_out, and_4_out);
  and and_4 (and_4_out, A[31], ~B[31], ~Adder_s[31]);  // And
  Multiplexer #(.Bits(32)) multiplexer_2 (
    .sel(and_1_out), .in_0({32{1'b0}}), .in_1(multiplexer_1_out), .out(multiplexer_2_out));
  Multiplexer #(.Bits(32)) multiplexer_3 (.sel(and_2_out), .in_0({32{1'b0}}), .in_1(A), .out(multiplexer_3_out));
  Sub #(.Bits(32)) sub_1 (.a(mul_1_mul_2), .b(multiplexer_2_out), .c_i(1'b0), .s(sub_1_s));  // open: c_o
  xor xor_1 (xor_1_out[0], or_5_out, Adder_s[31]);
  Add #(.Bits(32)) Adder (.a(A), .b(multiplexer_1_out), .c_i(or_4_out), .s(Adder_s), .c_o(Adder_c_o));
  assign and_5_out = A & multiplexer_1_out;  // And and_5, 32 bits wide
  assign or_6_out = A | multiplexer_1_out;  // Or or_6, 32 bits wide
  assign xor_2_out = A ^ multiplexer_1_out;  // XOr xor_2, 32 bits wide
  SLL sll_1 (.in(A), .shift(multiplexer_1_out[4:0]), .out(sll_1_out));
  SRL srl_1 (.in(A), .shift(multiplexer_1_out[4:0]), .out(srl_1_out));
  SRA sra_1 (.in(A), .shift(multiplexer_1_out[4:0]), .out(sra_1_out));
  Sub #(.Bits(32)) sub_2 (.a(sub_1_s), .b(multiplexer_3_out), .c_i(1'b0), .s(sub_2_s));  // open: c_o
  not not_2 (not_2_out[0], Adder_c_o);
  Multiplexer #(.Bits(32)) multiplexer_4 (
    .sel(and_6_out), .in_0({{31{1'b0}}, not_2_out[0]}), .in_1({{31{1'b0}}, xor_1_out[0]}),
    .out({multiplexer_4_out, Flags[0]}));
  and and_6 (and_6_out, ~OPSELECT[3], OPSELECT[2], OPSELECT[1], ~OPSELECT[0]);  // And
  nor nor_1 (Flags[1], Adder_s[31], Adder_s[30], Adder_s[29], Adder_s[28], Adder_s[27], Adder_s[26], Adder_s[25], Adder_s[24], Adder_s[23], Adder_s[22], Adder_s[21], Adder_s[20], Adder_s[19], Adder_s[18], Adder_s[17], Adder_s[16], Adder_s[15], Adder_s[14], Adder_s[13], Adder_s[12], Adder_s[11], Adder_s[10], Adder_s[9], Adder_s[8], Adder_s[7], Adder_s[6], Adder_s[5], Adder_s[4], Adder_s[3], Adder_s[2], Adder_s[1], Adder_s[0]);
  Multiplexer #(.Selector_Bits(5), .Bits(32)) multiplexer_5 (
    .sel(OPSELECT), .in_0(Adder_s), .in_1(Adder_s), .in_2(and_5_out), .in_3(or_6_out), .in_4(xor_2_out),
    .in_5({{31{1'b0}}, not_2_out[0]}), .in_6({{31{1'b0}}, xor_1_out[0]}), .in_7(sll_1_out), .in_8(srl_1_out),
    .in_9(sra_1_out), .in_10(mul_1_mul), .in_11(sub_2_s), .in_12(sub_2_s), .in_13(sub_2_s),
    .in_14({32{1'b0}}), .in_15({32{1'b0}}), .in_16({32{1'b0}}), .in_17({32{1'b0}}), .in_18({32{1'b0}}),
    .in_19({32{1'b0}}), .in_20({32{1'b0}}), .in_21({32{1'b0}}), .in_22({32{1'b0}}), .in_23({32{1'b0}}),
    .in_24({32{1'b0}}), .in_25({32{1'b0}}), .in_26({32{1'b0}}), .in_27({32{1'b0}}), .in_28({32{1'b0}}),
    .in_29({32{1'b0}}), .in_30({32{1'b0}}), .in_31({32{1'b0}}), .out(O));
  // Pins of 4 and 5 bits meet at OPSELECT

  // Notes on the sheet:
  //   OPSELECT: 0000:add
  //   0001:sub
  //   0010:and
  //   0011:or
  //   0100:xor
  //   0101:comUnsigned
  //   0110:comSigned
  //   0111:SLL
  //   1000:SRL
  //   1001:SRA
  //   Flags: Z, LessThan
  //   00000:add
  //   00001:sub
  //   00010:and
  //   00011:or
  //   00100:xor
  //   00101:comUnsigned
  //   00110:comSigned
  //   00111:SLL
  //   01000:SRL
  //   01001:SRA
  //   01010: MUL
  //   01011: MULH
  //   01100: MULHU
  //   01101: MULHSU
  //   01110: DIV
  //   01111: DIVU
  //   10000: REM
  //   10001: REMU
endmodule
