// Digital circuit AddressSpace.dig as structural Verilog
module AddressSpace (
  input  [31:0] Ain,
  output [2:0] Enable
);

  nor nor_1 (Enable[0], Ain[18], Ain[19], Ain[20], Ain[21], Ain[22], Ain[23], Ain[24], Ain[25], Ain[26], Ain[27], Ain[28], Ain[29], Ain[30], Ain[31]);
  nor nor_2 (Enable[1], ~Ain[18], Ain[19], Ain[20], Ain[21], Ain[22], Ain[23], Ain[24], Ain[25], Ain[26], Ain[27], Ain[28], Ain[29], Ain[30], Ain[31]);  // NOr
  nor nor_3 (Enable[2], Enable[0], Enable[1]);

  // Notes on the sheet:
  //   ROM:
  //   00000000
  //   0003FFFF
  //   RAM:
  //   00040000
  //   0007FFFF
  //   IO:
  //   00080000
endmodule
