// Digital circuit ControlLogic.dig as structural Verilog
module ControlLogic (
  input  [6:0] funct7,
  input  [2:0] funct3,
  input  [6:0] opcode,
  output [2:0] InsTypeSel,
  output [1:0] BrInsSel,
  output [1:0] PCInSel,
  output DSigned,
  output DHalf,
  output DByte,
  output [4:0] ALUOpSel,
  output ALUInSel,
  output [2:0] RegInSel,
  output RegWe,
  output MemWe
);

  wire and_1_out, decoder_1_out_1;
  wire [3:0] multiplexer_1_out, multiplexer_2_out, multiplexer_3_out, multiplexer_4_out;
  wire [5:5] undriven;
  wire [12:11] INS_Logic_d;

  and and_1 (and_1_out, decoder_1_out_1, funct7[5]);
  Multiplexer #(.Bits(4)) multiplexer_1 (.sel(funct7[5]), .in_0(4'b1000), .in_1(4'b1001), .out(multiplexer_1_out));
  ROM #(.AddrBits(5), .Bits(13)) INS_Logic (
    .A(opcode[6:2]), .sel(1'b1), .D({INS_Logic_d, InsTypeSel, PCInSel, ALUInSel, RegInSel, RegWe, MemWe}));
  Multiplexer #(.Bits(4)) multiplexer_2 (.sel(and_1_out), .in_0(4'b0000), .in_1(4'b0001), .out(multiplexer_2_out));
  ROM #(.AddrBits(6), .Bits(5)) ALUOP (.A({undriven[5], funct3, funct7[5], funct7[0]}), .sel(1'b1));  // open: D
  Multiplexer #(.Selector_Bits(3), .Bits(4)) multiplexer_3 (
    .sel(funct3), .in_0(multiplexer_2_out), .in_1(4'b0111), .in_2(4'b0110), .in_3(4'b0101), .in_4(4'b0100),
    .in_5(multiplexer_1_out), .in_6(4'b0011), .in_7(4'b0010), .out(multiplexer_3_out));
  Decoder #(.Selector_Bits(2)) decoder_1 (.sel(INS_Logic_d), .out_1(decoder_1_out_1));  // open: out_0, out_2, out_3
  Multiplexer #(.Bits(4)) multiplexer_4 (.sel(funct3[1]), .in_0(4'b0110), .in_1(4'b0101), .out(multiplexer_4_out));
  Multiplexer #(.Selector_Bits(2), .Bits(4)) multiplexer_5 (
    .sel(INS_Logic_d), .in_0(multiplexer_3_out), .in_1(multiplexer_3_out), .in_2(4'b0000),
    .in_3(multiplexer_4_out), .out(ALUOpSel[3:0]));
  not not_1 (DSigned, funct3[2]);
  Decoder #(.Selector_Bits(2)) decoder_2 (.sel(funct3[1:0]), .out_0(DByte), .out_1(DHalf));  // open: out_2, out_3
  // Pins of 4 and 5 bits meet at {5{1'b0}}
  // Pins of 4 and 5 bits meet at 5'b00110
  // Pins of 4 and 5 bits meet at 5'b00101
  // Pins of 5 and 6 bits meet at {undriven[5], funct3, funct7[5], funct7[0]}

  assign ALUOpSel[4] = 1'b0;
  assign BrInsSel = {funct3[2], funct3[0]};

  // Notes on the sheet:
  //   InsTypeSel: 000: I
  //   001: S
  //   010: B
  //   011: U
  //   100: J
  //   BrInsSel: 00: BEQ
  //   01: BNE
  //   10: BLT
  //   11: BGE
  //   Reg in select
  //   000: ALU
  //   001: RAM
  //   010: PC+4
  //   011: Imm
  //   100: Ad Add
  //   ALU in select
  //   0: rs2
  //   1: Imm
  //   contents of INS_Logic (hex, n*v repeats v):
  //   5*0,312,7*0,30e
  //   contents of ALUOP (hex, n*v repeats v):
  //   4*0,7,0,0,0,4*6,4*5
  //   PC in select
  //   00: PC+4
  //   01: Ad Adder
  //   10: ALU
  //   11: Con Bra
  //   Ins Type
  //   000: I
  //   001: S
  //   010: B
  //   011: U
  //   100: J
  //   ALU Reg?
  //   ALU op
  //   00: Imm
  //   01: Reg
  //   10: Add
  //   11: Conditional Branch
  //   ALU op
  //   00000:add
  //   00001:sub
  //   00010:and
  //   00011:or
  //   00100:xor
  //   00101:comUnsigned
  //   00110:comSigned
  //   00111:SLL
  //   01000:SRL
  //   01001:SRA
  //   01010: MUL
  //   01011: MULH
  //   01100: MULHU
  //   01101: MULHSU
  //   01110: DIV
  //   01111: DIVU
  //   10000: REM
  //   10001: REMU
endmodule
