// Digital circuit MemoryMapperExp.dig as structural Verilog
module MemoryMapperExp (
  input  Stall,
  input  Clock,
  input  [31:0] Din,
  input  [31:0] Ain,
  input  [31:0] INSAin,
  input  [5:0] ByteSelect,
  input  We,
  input  [2:0] RegInsel,
  input  [31:0] DrIO,
  output [31:0] INSout,
  output [31:0] Dout,
  output [31:0] AddIO,
  output [31:0] DwIO,
  output [3:0] WeIO,
  output ReIO,
  output CLKIO
);

  wire and_1_out, and_2_out, decoder_1_out_1, nor_1_out, rs_1_q;
  wire [2:0] addressspace_1_enable, addressspace_2_enable;
  wire [3:0] bitextender_1_out;
  wire [7:0] multiplexer_1_out, multiplexer_3_out;
  wire [31:0] INSROM_d, multiplexer_7_out, ram_256kb_1_dout, ram_256kb_1_insout, RROM_d;

  AddressSpace addressspace_1 (.Ain(Ain), .Enable(addressspace_1_enable));
  AddressSpace addressspace_2 (.Ain(INSAin), .Enable(addressspace_2_enable));
  Decoder #(.Selector_Bits(3)) decoder_1 (
    .sel(RegInsel), .out_1(decoder_1_out_1));  // open: out_0, out_2, out_3, out_4, out_5, out_6, out_7
  and and_1 (and_1_out, We, addressspace_1_enable[1]);
  and and_2 (and_2_out, We, addressspace_1_enable[2]);
  and and_3 (ReIO, addressspace_1_enable[2], decoder_1_out_1);
  BitExtender #(.inputBits(1), .outputBits(4)) bitextender_1 (.in(and_2_out), .out(bitextender_1_out));
  assign WeIO = bitextender_1_out & ByteSelect[3:0];  // And and_4, 4 bits wide
  Multiplexer #(.Bits(8)) multiplexer_1 (
    .sel(ByteSelect[4]), .in_0(Din[31:24]), .in_1(Din[7:0]), .out(multiplexer_1_out));
  Multiplexer #(.Bits(8)) multiplexer_2 (.sel(ByteSelect[4]), .in_0(Din[15:8]), .in_1(Din[7:0]), .out(DwIO[15:8]));
  Multiplexer #(.Bits(8)) multiplexer_3 (
    .sel(ByteSelect[4]), .in_0(Din[23:16]), .in_1(Din[7:0]), .out(multiplexer_3_out));
  Multiplexer #(.Bits(8)) multiplexer_4 (
    .sel(ByteSelect[5]), .in_0(multiplexer_1_out), .in_1(DwIO[15:8]), .out(DwIO[31:24]));
  nor nor_1 (nor_1_out, Stall, Clock);
  Multiplexer #(.Bits(8)) multiplexer_5 (
    .sel(ByteSelect[5]), .in_0(multiplexer_3_out), .in_1(Din[7:0]), .out(DwIO[23:16]));
  rs rs_1 (.s(Stall), .r(nor_1_out), .q(rs_1_q));  // open: nq
  and and_5 (CLKIO, Clock, ~rs_1_q);  // And
  ROM #(.AddrBits(11), .isProgramMemory("true"), .Bits(32)) RROM (.A(Ain[12:2]), .sel(1'b1), .D(RROM_d));
  ROM #(.AddrBits(11), .isProgramMemory("true"), .Bits(32)) INSROM (.A(INSAin[12:2]), .sel(1'b1), .D(INSROM_d));
  RAM_256KB ram_256kb_1 (
    .INSAddressIn(INSAin[17:2]), .ByteSelect(ByteSelect), .AddressIn(Ain[17:2]),
    .Din({DwIO[31:8], Din[7:0]}), .We(and_1_out), .Clock(CLKIO), .Dout(ram_256kb_1_dout),
    .INSout(ram_256kb_1_insout));
  Multiplexer #(.Bits(32)) multiplexer_6 (
    .sel(addressspace_2_enable[1]), .in_0(INSROM_d), .in_1(ram_256kb_1_insout), .out(INSout));
  Multiplexer #(.Bits(32)) multiplexer_7 (
    .sel(addressspace_1_enable[1]), .in_0(RROM_d), .in_1(ram_256kb_1_dout), .out(multiplexer_7_out));
  Multiplexer #(.Bits(32)) multiplexer_8 (
    .sel(addressspace_1_enable[2]), .in_0(multiplexer_7_out), .in_1(DrIO), .out(Dout));

  assign AddIO = Ain;
  assign DwIO[7:0] = Din[7:0];

  // Notes on the sheet:
  //   RROM loads visual_wozmon.intel.hex
  //   INSROM loads visual_wozmon.intel.hex
endmodule
