// Digital circuit ProgramCounter.dig as structural Verilog
module ProgramCounter (
  input  Stall,
  input  Clock,
  input  [31:0] Din,
  output [31:0] Dout,
  output [31:0] PC_plus_4
);

  wire and_1_out, nor_1_out, rs_1_q;

  nor nor_1 (nor_1_out, Stall, Clock);
  rs rs_1 (.s(Stall), .r(nor_1_out), .q(rs_1_q));  // open: nq
  and and_1 (and_1_out, Clock, ~rs_1_q);  // And
  Register #(.Bits(32), .isProgramCounter("true")) register_1 (
    .D({Din[31:1], 1'b0}), .C(and_1_out), .en(1'b1), .Q(Dout));
  Add #(.Bits(32)) add_1 (.a(Dout), .b(32'h4), .c_i(1'b0), .s(PC_plus_4));  // open: c_o
endmodule
