// Digital circuit RAM_256KB.dig as structural Verilog
module RAM_256KB (
  input  [15:0] INSAddressIn,
  input  [5:0] ByteSelect,
  input  [15:0] AddressIn,
  input  [31:0] Din,
  input  We,
  input  Clock,
  output [31:0] Dout,
  output [31:0] INSout
);

  wire [3:0] and_1_out, bitextender_1_out;

  BitExtender #(.inputBits(1), .outputBits(4)) bitextender_1 (.in(We), .out(bitextender_1_out));
  assign and_1_out = bitextender_1_out & ByteSelect[3:0];  // And and_1, 4 bits wide
  RAMDualAccess #(.AddrBits(16), .Bits(8)) ramdualaccess_1 (
    .str(and_1_out[0]), .C(Clock), .ld(1'b1), .A1(AddressIn), .Din1(Din[7:0]), .A2(INSAddressIn),
    .D1(Dout[7:0]), .D2(INSout[7:0]));
  RAMDualAccess #(.AddrBits(16), .Bits(8)) ramdualaccess_2 (
    .str(and_1_out[1]), .C(Clock), .ld(1'b1), .A1(AddressIn), .Din1(Din[15:8]), .A2(INSAddressIn),
    .D1(Dout[15:8]), .D2(INSout[15:8]));
  RAMDualAccess #(.AddrBits(16), .Bits(8)) ramdualaccess_3 (
    .str(and_1_out[2]), .C(Clock), .ld(1'b1), .A1(AddressIn), .Din1(Din[23:16]), .A2(INSAddressIn),
    .D1(Dout[23:16]), .D2(INSout[23:16]));
  RAMDualAccess #(.AddrBits(16), .Bits(8)) ramdualaccess_4 (
    .str(and_1_out[3]), .C(Clock), .ld(1'b1), .A1(AddressIn), .Din1(Din[31:24]), .A2(INSAddressIn),
    .D1(Dout[31:24]), .D2(INSout[31:24]));
endmodule
