// Digital circuit Registers.dig as structural Verilog
module Registers (
  input  Stall,
  input  Clock,
  input  [31:0] Din,
  input  We,
  input  [4:0] rs1,
  input  [4:0] rs2,
  input  [4:0] rd,
  output [31:0] rs1O,
  output [31:0] rs2O
);

  wire and_1_out, and_2_out, nor_1_out, nor_2_out, nor_3_out, or_1_out, rs_1_q;
  wire [31:0] Registers_1_31_da, Registers_1_31_db;

  nor nor_1 (nor_1_out, Stall, Clock);
  rs rs_1 (.s(Stall), .r(nor_1_out), .q(rs_1_q));  // open: nq
  or or_1 (or_1_out, rd[0], rd[1], rd[2], rd[3], rd[4]);
  and and_1 (and_1_out, We, or_1_out);
  and and_2 (and_2_out, Clock, ~rs_1_q);  // And
  RegisterFile #(.AddrBits(5), .Bits(32)) Registers_1_31 (
    .Din(Din), .we(and_1_out), .Rw(rd), .C(and_2_out), .Ra(rs1), .Rb(rs2), .Da(Registers_1_31_da),
    .Db(Registers_1_31_db));
  nor nor_2 (nor_2_out, rs1[0], rs1[1], rs1[2], rs1[3], rs1[4]);
  nor nor_3 (nor_3_out, rs2[0], rs2[1], rs2[2], rs2[3], rs2[4]);
  Multiplexer #(.Bits(32)) multiplexer_1 (.sel(nor_2_out), .in_0(Registers_1_31_da), .in_1({32{1'b0}}), .out(rs1O));
  Multiplexer #(.Bits(32)) multiplexer_2 (.sel(nor_3_out), .in_0(Registers_1_31_db), .in_1({32{1'b0}}), .out(rs2O));
endmodule
