// Digital circuit SRA.dig as structural Verilog
module SRA (
  input  [31:0] in,
  input  [4:0] shift,
  output [31:0] out
);

  wire [1:0] bitextender_1_out;
  wire [3:0] bitextender_2_out;
  wire [7:0] bitextender_3_out;
  wire [15:0] bitextender_4_out;
  wire [31:0] multiplexer_1_out, multiplexer_2_out, multiplexer_3_out, multiplexer_4_out;

  Multiplexer #(.Bits(32)) multiplexer_1 (
    .sel(shift[0]), .in_0(in), .in_1({{2{in[31]}}, in[30:1]}), .out(multiplexer_1_out));
  BitExtender #(.inputBits(1), .outputBits(2)) bitextender_1 (.in(in[31]), .out(bitextender_1_out));
  Multiplexer #(.Bits(32)) multiplexer_2 (
    .sel(shift[1]), .in_0(multiplexer_1_out), .in_1({bitextender_1_out, multiplexer_1_out[31:2]}),
    .out(multiplexer_2_out));
  BitExtender #(.inputBits(1), .outputBits(4)) bitextender_2 (.in(in[31]), .out(bitextender_2_out));
  Multiplexer #(.Bits(32)) multiplexer_3 (
    .sel(shift[2]), .in_0(multiplexer_2_out), .in_1({bitextender_2_out, multiplexer_2_out[31:4]}),
    .out(multiplexer_3_out));
  BitExtender #(.inputBits(1), .outputBits(8)) bitextender_3 (.in(in[31]), .out(bitextender_3_out));
  Multiplexer #(.Bits(32)) multiplexer_4 (
    .sel(shift[3]), .in_0(multiplexer_3_out), .in_1({bitextender_3_out, multiplexer_3_out[31:8]}),
    .out(multiplexer_4_out));
  BitExtender #(.inputBits(1)) bitextender_4 (.in(in[31]), .out(bitextender_4_out));
  Multiplexer #(.Bits(32)) multiplexer_5 (
    .sel(shift[4]), .in_0(multiplexer_4_out), .in_1({bitextender_4_out, multiplexer_4_out[31:16]}), .out(out));
endmodule
