// Digital circuit SRL.dig as structural Verilog
module SRL (
  input  [31:0] in,
  input  [4:0] shift,
  output [31:0] out
);

  wire [31:0] multiplexer_1_out, multiplexer_2_out, multiplexer_3_out, multiplexer_4_out;

  Multiplexer #(.Bits(32)) multiplexer_1 (.sel(shift[0]), .in_0(in), .in_1({1'b0, in[31:1]}), .out(multiplexer_1_out));
  Multiplexer #(.Bits(32)) multiplexer_2 (
    .sel(shift[1]), .in_0(multiplexer_1_out), .in_1({2'b00, multiplexer_1_out[31:2]}), .out(multiplexer_2_out));
  Multiplexer #(.Bits(32)) multiplexer_3 (
    .sel(shift[2]), .in_0(multiplexer_2_out), .in_1({4'b0000, multiplexer_2_out[31:4]}),
    .out(multiplexer_3_out));
  Multiplexer #(.Bits(32)) multiplexer_4 (
    .sel(shift[3]), .in_0(multiplexer_3_out), .in_1({{8{1'b0}}, multiplexer_3_out[31:8]}),
    .out(multiplexer_4_out));
  Multiplexer #(.Bits(32)) multiplexer_5 (
    .sel(shift[4]), .in_0(multiplexer_4_out), .in_1({{16{1'b0}}, multiplexer_4_out[31:16]}), .out(out));
endmodule
