// Digital circuit UnsignedDivider.dig as structural Verilog
module UnsignedDivider (
  input  [31:0] A,
  input  [31:0] B,
  output [31:0] q,
  output [31:0] rem
);

  wire divstage_1_p3, divstage_2_p3, divstage_3_p3, divstage_4_p3, divstage_5_p3, divstage_6_p3,
       divstage_7_p3, divstage_8_p3, divstage_9_p3, divstage_10_p3, divstage_11_p3, divstage_12_p3,
       divstage_13_p3, divstage_14_p3, divstage_15_p3, divstage_16_p3, divstage_17_p3, divstage_18_p3,
       divstage_19_p3, divstage_20_p3, divstage_21_p3, divstage_22_p3, divstage_23_p3, divstage_24_p3,
       divstage_25_p3, divstage_26_p3, divstage_27_p3, divstage_28_p3, divstage_29_p3, divstage_30_p3,
       divstage_31_p3;

  // divstage divstage_1: pin names not known; wires that end beside it: B, A[0], divstage_1_p3, rem, q[0]
  // divstage divstage_2: pin names not known; wires that end beside it: B, A[1], divstage_2_p3, divstage_1_p3, q[1]
  // divstage divstage_3: pin names not known; wires that end beside it: B, A[2], divstage_3_p3, divstage_2_p3, q[2]
  // divstage divstage_4: pin names not known; wires that end beside it: B, A[3], divstage_4_p3, divstage_3_p3, q[3]
  // divstage divstage_5: pin names not known; wires that end beside it: B, A[4], divstage_5_p3, divstage_4_p3, q[4]
  // divstage divstage_6: pin names not known; wires that end beside it: B, A[5], divstage_6_p3, divstage_5_p3, q[5]
  // divstage divstage_7: pin names not known; wires that end beside it: B, A[6], divstage_7_p3, divstage_6_p3, q[6]
  // divstage divstage_8: pin names not known; wires that end beside it: B, A[7], divstage_8_p3, divstage_7_p3, q[7]
  // divstage divstage_9: pin names not known; wires that end beside it: B, A[8], divstage_9_p3, divstage_8_p3, q[8]
  // divstage divstage_10: pin names not known; wires that end beside it: B, A[9], divstage_10_p3, divstage_9_p3, q[9]
  // divstage divstage_11: pin names not known; wires that end beside it: B, A[10], divstage_11_p3, divstage_10_p3, q[10]
  // divstage divstage_12: pin names not known; wires that end beside it: B, A[11], divstage_12_p3, divstage_11_p3, q[11]
  // divstage divstage_13: pin names not known; wires that end beside it: B, A[12], divstage_13_p3, divstage_12_p3, q[12]
  // divstage divstage_14: pin names not known; wires that end beside it: B, A[13], divstage_14_p3, divstage_13_p3, q[13]
  // divstage divstage_15: pin names not known; wires that end beside it: B, A[14], divstage_15_p3, divstage_14_p3, q[14]
  // divstage divstage_16: pin names not known; wires that end beside it: B, A[15], divstage_16_p3, divstage_15_p3, q[15]
  // divstage divstage_17: pin names not known; wires that end beside it: B, A[16], divstage_17_p3, divstage_16_p3, q[16]
  // divstage divstage_18: pin names not known; wires that end beside it: B, A[17], divstage_18_p3, divstage_17_p3, q[17]
  // divstage divstage_19: pin names not known; wires that end beside it: B, A[18], divstage_19_p3, divstage_18_p3, q[18]
  // divstage divstage_20: pin names not known; wires that end beside it: B, A[19], divstage_20_p3, divstage_19_p3, q[19]
  // divstage divstage_21: pin names not known; wires that end beside it: B, A[20], divstage_21_p3, divstage_20_p3, q[20]
  // divstage divstage_22: pin names not known; wires that end beside it: B, A[21], divstage_22_p3, divstage_21_p3, q[21]
  // divstage divstage_23: pin names not known; wires that end beside it: B, A[22], divstage_23_p3, divstage_22_p3, q[22]
  // divstage divstage_24: pin names not known; wires that end beside it: B, A[23], divstage_24_p3, divstage_23_p3, q[23]
  // divstage divstage_25: pin names not known; wires that end beside it: B, A[24], divstage_25_p3, divstage_24_p3, q[24]
  // divstage divstage_26: pin names not known; wires that end beside it: B, A[25], divstage_26_p3, divstage_25_p3, q[25]
  // divstage divstage_27: pin names not known; wires that end beside it: B, A[26], divstage_27_p3, divstage_26_p3, q[26]
  // divstage divstage_28: pin names not known; wires that end beside it: B, A[27], divstage_28_p3, divstage_27_p3, q[27]
  // divstage divstage_29: pin names not known; wires that end beside it: B, A[28], divstage_29_p3, divstage_28_p3, q[28]
  // divstage divstage_30: pin names not known; wires that end beside it: B, A[29], divstage_30_p3, divstage_29_p3, q[29]
  // divstage divstage_31: pin names not known; wires that end beside it: B, A[30], divstage_31_p3, divstage_30_p3, q[30]
  // divstage divstage_32: pin names not known; wires that end beside it: B, A[31], {32{1'b0}}, divstage_31_p3, q[31]
endmodule
