// Digital circuit bram.dig as structural Verilog
module bram (
  input  str,
  input  c,
  input  ld,
  input  [15:0] _1a,
  input  [7:0] _1din,
  input  [15:0] _2a,
  output [7:0] _1d,
  output [7:0] _2d
);

  wire not_1_out;
  wire [7:0] ramdualaccess_1_d1, ramdualaccess_1_d2;

  RAMDualAccess #(.AddrBits(16), .Bits(8)) ramdualaccess_1 (
    .str(str), .C(c), .ld(ld), .A1(_1a), .Din1(_1din), .A2(_2a), .D1(ramdualaccess_1_d1),
    .D2(ramdualaccess_1_d2));
  not not_1 (not_1_out, c);
  Register #(.Bits(8)) register_1 (.D(ramdualaccess_1_d1), .C(not_1_out), .en(1'b1), .Q(_1d));
  Register #(.Bits(8)) register_2 (.D(ramdualaccess_1_d2), .C(not_1_out), .en(1'b1), .Q(_2d));
endmodule
