// Digital circuit divstage.dig as structural Verilog
module divstage (
  input  [31:0] remin,
  input  bitin,
  input  [31:0] divisor,
  output [31:0] remo,
  output qbit
);

  wire comparator_1_lt;
  wire [31:0] sub_1_s;

  Sub #(.Bits(32)) sub_1 (.a({remin[30:0], bitin}), .b(divisor), .c_i(comparator_1_lt), .s(sub_1_s));  // open: c_o
  Comparator #(.Bits(32)) comparator_1 (.a({remin[30:0], bitin}), .b(divisor), .lt(comparator_1_lt));  // open: gt, eq
  not not_1 (qbit, comparator_1_lt);
  Multiplexer #(.Bits(32)) multiplexer_1 (
    .sel(comparator_1_lt), .in_0(sub_1_s), .in_1({remin[30:0], bitin}), .out(remo));
endmodule
