// Digital circuit main_cpu.dig as structural Verilog
module main_cpu (
  input  CLK
);

  wire controllogic_1_aluinsel, controllogic_1_dbyte, controllogic_1_dhalf, controllogic_1_dsigned,
       controllogic_1_memwe, controllogic_1_regwe;
  wire [1:0] alu_1_flags, controllogic_1_brinssel, controllogic_1_pcinsel;
  wire [2:0] controllogic_1_instypesel, controllogic_1_reginsel, instructionsplicer_1_funct3;
  wire [3:0] controllogic_1_aluopsel, datacontroller_1_byteselect;
  wire [4:0] instructionsplicer_1_rd, instructionsplicer_1_rs1, instructionsplicer_1_rs2;
  wire [6:0] instructionsplicer_1_funct7, instructionsplicer_1_opcode;
  wire [31:0] add_1_s, alu_1_o, datacontroller_1_addressout, datacontroller_1_docpu,
       instructionsplicer_1_imm, memorymapper_1_dout, memorymapper_1_insout, multiplexer_1_out,
       multiplexer_2_out, pcinselector_1_pc, programcounter_1_dout, programcounter_1_pc_plus_4,
       registers_1_rs1o, registers_1_rs2o;

  PcInSelector pcinselector_1 (
    .BranchIns(controllogic_1_brinssel), .PcInSel(controllogic_1_pcinsel), .Flags(alu_1_flags),
    .ALU(alu_1_o), .AdAdd(add_1_s), .PC_plus_4(programcounter_1_pc_plus_4), .PC(pcinselector_1_pc));
  DataController datacontroller_1 (
    .AddressIn(alu_1_o), .DinMMU(memorymapper_1_dout), .Signed(controllogic_1_dsigned),
    .half(controllogic_1_dhalf), .isbyte(controllogic_1_dbyte), .AddressOut(datacontroller_1_addressout),
    .DoCPU(datacontroller_1_docpu), .ByteSelect(datacontroller_1_byteselect));
  ProgramCounter programcounter_1 (
    .Clock(CLK), .Din(pcinselector_1_pc), .Dout(programcounter_1_dout), .PC_plus_4(programcounter_1_pc_plus_4));
  Add #(.Bits(32)) add_1 (
    .a(instructionsplicer_1_imm), .b(programcounter_1_dout), .c_i(1'b0), .s(add_1_s));  // open: c_o
  ALU alu_1 (
    .OPSELECT(controllogic_1_aluopsel), .B(multiplexer_1_out), .A(registers_1_rs1o), .O(alu_1_o),
    .Flags(alu_1_flags));
  Multiplexer #(.Bits(32)) multiplexer_1 (
    .sel(controllogic_1_aluinsel), .in_0(registers_1_rs2o), .in_1(instructionsplicer_1_imm),
    .out(multiplexer_1_out));
  Multiplexer #(.Selector_Bits(3), .Bits(32)) multiplexer_2 (
    .sel(controllogic_1_reginsel), .in_0(alu_1_o), .in_1(datacontroller_1_docpu),
    .in_2(programcounter_1_pc_plus_4), .in_3(instructionsplicer_1_imm), .in_4(add_1_s), .in_5({32{1'b0}}),
    .in_6({32{1'b0}}), .in_7({32{1'b0}}), .out(multiplexer_2_out));
  Registers registers_1 (
    .clk(CLK), .Din(multiplexer_2_out), .We(controllogic_1_regwe), .rs1(instructionsplicer_1_rs1),
    .rs2(instructionsplicer_1_rs2), .rd(instructionsplicer_1_rd), .rs1O(registers_1_rs1o),
    .rs2O(registers_1_rs2o));
  MemoryMapper memorymapper_1 (
    .Clock(CLK), .Din(registers_1_rs2o), .Ain(datacontroller_1_addressout), .INSAin(programcounter_1_dout),
    .ByteSelect(datacontroller_1_byteselect), .We(controllogic_1_memwe), .RegInsel(controllogic_1_reginsel),
    .INSout(memorymapper_1_insout), .Dout(memorymapper_1_dout));
  ControlLogic controllogic_1 (
    .funct7(instructionsplicer_1_funct7), .funct3(instructionsplicer_1_funct3),
    .opcode(instructionsplicer_1_opcode), .InsTypeSel(controllogic_1_instypesel),
    .BrInsSel(controllogic_1_brinssel), .PCInSel(controllogic_1_pcinsel), .DSigned(controllogic_1_dsigned),
    .DHalf(controllogic_1_dhalf), .DByte(controllogic_1_dbyte), .ALUOpSel(controllogic_1_aluopsel),
    .ALUInSel(controllogic_1_aluinsel), .RegInSel(controllogic_1_reginsel), .RegWe(controllogic_1_regwe),
    .MemWe(controllogic_1_memwe));
  InstructionSplicer instructionsplicer_1 (
    .ImmSel(controllogic_1_instypesel), .INSin(memorymapper_1_insout), .funct7(instructionsplicer_1_funct7),
    .funct3(instructionsplicer_1_funct3), .opcode(instructionsplicer_1_opcode),
    .rs1(instructionsplicer_1_rs1), .rs2(instructionsplicer_1_rs2), .rd(instructionsplicer_1_rd),
    .Imm(instructionsplicer_1_imm));

  // Notes on the sheet:
  //   CLK: Hz: 75000
  //   PC Lines
  //   Data Controller Lines
  //   ALU Lines
  //   Register Lines
  //   Memory Mapper Lines
endmodule
