// Digital circuit main_cpu_exp.dig as structural Verilog
module main_cpu_exp (
  input  CLK,
  input  [31:0] DrIO,
  output [31:0] AddIO,
  output [31:0] DwIO,
  output [3:0] WeIO,
  output ReIO,
  output CLKIO
);

  wire alu_1_p1, alu_1_p7, alu_1_p9, controllogic_1_aluinsel, controllogic_1_regwe, datacontroller_1_p2,
       datacontroller_1_p3, datacontroller_1_p4, datacontroller_1_p5, memorymapperexp_1_p7;
  wire [1:0] alu_1_p2, controllogic_1_brinssel, controllogic_1_pcinsel;
  wire [2:0] controllogic_1_instypesel, instructionsplicer_1_funct3, memorymapperexp_1_p8;
  wire [4:0] alu_1_p6, instructionsplicer_1_rd, instructionsplicer_1_rs1, instructionsplicer_1_rs2;
  wire [6:0] instructionsplicer_1_funct7, instructionsplicer_1_opcode;
  wire [31:0] add_1_s, alu_1_p4, alu_1_p5, alu_1_p8, datacontroller_1_p1, instructionsplicer_1_imm,
       memorymapperexp_1_p10, multiplexer_2_out, pcinselector_1_pc, programcounter_1_dout,
       programcounter_1_pc_plus_4, registers_1_rs2o;

  PcInSelector pcinselector_1 (
    .BranchIns(controllogic_1_brinssel), .PcInSel(controllogic_1_pcinsel), .Flags(alu_1_p2),
    .ALU(datacontroller_1_p1), .AdAdd(add_1_s), .PC_plus_4(programcounter_1_pc_plus_4), .PC(pcinselector_1_pc));
  // DataController datacontroller_1: pin names not known; wires that end beside it: datacontroller_1_p1, datacontroller_1_p2, datacontroller_1_p3, datacontroller_1_p4, datacontroller_1_p5
  ProgramCounter programcounter_1 (
    .Stall(alu_1_p1), .Clock(CLK), .Din(pcinselector_1_pc), .Dout(programcounter_1_dout),
    .PC_plus_4(programcounter_1_pc_plus_4));
  Add #(.Bits(32)) add_1 (
    .a(instructionsplicer_1_imm), .b(programcounter_1_dout), .c_i(1'b0), .s(add_1_s));  // open: c_o
  // ALU alu_1: pin names not known; wires that end beside it: alu_1_p1, alu_1_p2, datacontroller_1_p1, alu_1_p4, alu_1_p5, alu_1_p6, alu_1_p7, alu_1_p8, alu_1_p9
  Multiplexer #(.Bits(32)) multiplexer_1 (
    .sel(controllogic_1_aluinsel), .in_0(registers_1_rs2o), .in_1(instructionsplicer_1_imm), .out(alu_1_p5));
  Multiplexer #(.Selector_Bits(3), .Bits(32)) multiplexer_2 (
    .sel(memorymapperexp_1_p8), .in_0(datacontroller_1_p1), .in_1(alu_1_p8),
    .in_2(programcounter_1_pc_plus_4), .in_3(instructionsplicer_1_imm), .in_4(add_1_s), .in_5({32{1'b0}}),
    .in_6({32{1'b0}}), .in_7({32{1'b0}}), .out(multiplexer_2_out));
  Registers registers_1 (
    .Stall(alu_1_p1), .Clock(CLK), .Din(multiplexer_2_out), .We(controllogic_1_regwe),
    .rs1(instructionsplicer_1_rs1), .rs2(instructionsplicer_1_rs2), .rd(instructionsplicer_1_rd),
    .rs1O(alu_1_p4), .rs2O(registers_1_rs2o));
  // MemoryMapperExp memorymapperexp_1: pin names not known; wires that end beside it: alu_1_p1, CLK, registers_1_rs2o, alu_1_p7, programcounter_1_dout, alu_1_p9, memorymapperexp_1_p7, memorymapperexp_1_p8, DrIO, memorymapperexp_1_p10, datacontroller_1_p2, AddIO, DwIO, WeIO, ReIO, CLKIO
  ControlLogic controllogic_1 (
    .funct7(instructionsplicer_1_funct7), .funct3(instructionsplicer_1_funct3),
    .opcode(instructionsplicer_1_opcode), .InsTypeSel(controllogic_1_instypesel),
    .BrInsSel(controllogic_1_brinssel), .PCInSel(controllogic_1_pcinsel), .DSigned(datacontroller_1_p3),
    .DHalf(datacontroller_1_p4), .DByte(datacontroller_1_p5), .ALUOpSel(alu_1_p6),
    .ALUInSel(controllogic_1_aluinsel), .RegInSel(memorymapperexp_1_p8), .RegWe(controllogic_1_regwe),
    .MemWe(memorymapperexp_1_p7));
  InstructionSplicer instructionsplicer_1 (
    .ImmSel(controllogic_1_instypesel), .INSin(memorymapperexp_1_p10), .funct7(instructionsplicer_1_funct7),
    .funct3(instructionsplicer_1_funct3), .opcode(instructionsplicer_1_opcode),
    .rs1(instructionsplicer_1_rs1), .rs2(instructionsplicer_1_rs2), .rd(instructionsplicer_1_rd),
    .Imm(instructionsplicer_1_imm));

  // Notes on the sheet:
  //   CLK: Hz: 30
  //   PC Lines
  //   Data Controller Lines
  //   ALU Lines
  //   Register Lines
  //   Memory Mapper Lines
endmodule
