// Digital circuit seq_div.dig as structural Verilog
module seq_div (
  input  [31:0] A,
  input  [31:0] B,
  input  clock,
  input  in_6,
  input  in_7,
  output [31:0] q,
  output [31:0] rem
);

  wire divstage_1_p3;
  wire [4:0] add_1_s, register_1_q;
  wire [31:0] divstage_2_p3, sll_1_out;

  Add #(.Bits(5)) add_1 (.a(5'b00010), .b(register_1_q), .c_i(1'b0), .s(add_1_s));  // open: c_o
  Register #(.Bits(5)) register_1 (.D(add_1_s), .C(clock), .en(1'b1), .Q(register_1_q));
  SLL sll_1 (.in(A), .shift(register_1_q), .out(sll_1_out));
  // divstage divstage_1: pin names not known; wires that end beside it: B, sll_1_out[30], divstage_1_p3, rem
  // divstage divstage_2: pin names not known; wires that end beside it: B, sll_1_out[31], divstage_2_p3, divstage_1_p3
  Register #(.Bits(32)) register_2 (.D(rem), .C(clock), .en(1'b1), .Q(divstage_2_p3));
  Register #(.Bits(32)) register_3 (.D({{28{1'b0}}, q[1:0], in_7, in_6}), .C(clock), .en(1'b1), .Q(q));
endmodule
