// Digital circuit divstage.dig as structural Verilog
module divstage (
  input  [31:0] divisor,
  input  bitin,
  input  [31:0] remin,
  output [31:0] remo,
  output qbit
);

  wire sub_1_c_o;
  wire [31:0] sub_1_s;

  Sub #(.Bits(32)) sub_1 (.a({remin[30:0], bitin}), .b(divisor), .c_i(1'b0), .s(sub_1_s), .c_o(sub_1_c_o));
  Multiplexer #(.Bits(32)) multiplexer_1 (.sel(sub_1_c_o), .in_0(sub_1_s), .in_1({remin[30:0], bitin}), .out(remo));
  not not_1 (qbit, sub_1_c_o);
endmodule
