// Digital circuit full_div.dig as structural Verilog
module full_div (
  input  [31:0] A,
  input  [31:0] B,
  input  s,
  input  r,
  input  clock,
  input  div,
  output [31:0] O,
  output stall
);

  wire and_1_out, and_2_out, comparator_1_eq, xor_1_out;
  wire [31:0] multiplexer_1_out, multiplexer_2_out, multiplexer_3_out, multiplexer_4_out, multiplexer_5_out,
       multiplexer_6_out, neg_1_out, neg_2_out, neg_3_out, neg_4_out, seq_div_1_q, seq_div_1_rem;

  Neg #(.Bits(32)) neg_1 (.in(B), .out(neg_1_out));
  and and_1 (and_1_out, A[31], s);
  and and_2 (and_2_out, B[31], s);
  Comparator #(.Bits(32)) comparator_1 (.a(B), .b({32{1'b0}}), .eq(comparator_1_eq));  // open: gt, lt
  Neg #(.Bits(32)) neg_2 (.in(A), .out(neg_2_out));
  Multiplexer #(.Bits(32)) multiplexer_1 (.sel(and_2_out), .in_0(B), .in_1(neg_1_out), .out(multiplexer_1_out));
  Multiplexer #(.Bits(32)) multiplexer_2 (.sel(and_1_out), .in_0(A), .in_1(neg_2_out), .out(multiplexer_2_out));
  xor xor_1 (xor_1_out, and_1_out, and_2_out);
  seq_div seq_div_1 (
    .clock(clock), .div(div), .A(multiplexer_2_out), .B(multiplexer_1_out), .stall(stall), .q(seq_div_1_q),
    .rem(seq_div_1_rem));
  Neg #(.Bits(32)) neg_3 (.in(seq_div_1_q), .out(neg_3_out));
  Neg #(.Bits(32)) neg_4 (.in(seq_div_1_rem), .out(neg_4_out));
  Multiplexer #(.Bits(32)) multiplexer_3 (
    .sel(xor_1_out), .in_0(seq_div_1_q), .in_1(neg_3_out), .out(multiplexer_3_out));
  Multiplexer #(.Bits(32)) multiplexer_4 (
    .sel(and_1_out), .in_0(seq_div_1_rem), .in_1(neg_4_out), .out(multiplexer_4_out));
  Multiplexer #(.Bits(32)) multiplexer_5 (
    .sel(comparator_1_eq), .in_0(multiplexer_3_out), .in_1({32{1'b1}}), .out(multiplexer_5_out));
  Multiplexer #(.Bits(32)) multiplexer_6 (
    .sel(comparator_1_eq), .in_0(multiplexer_4_out), .in_1(A), .out(multiplexer_6_out));
  Multiplexer #(.Bits(32)) multiplexer_7 (.sel(r), .in_0(multiplexer_5_out), .in_1(multiplexer_6_out), .out(O));
endmodule
