// Digital circuit mul.dig as structural Verilog
module mul (
  input  [31:0] A,
  input  [31:0] B,
  input  As,
  input  Bs,
  output [31:0] L,
  output [31:0] H
);

  wire and_1_out, and_2_out;
  wire [31:0] multiplexer_1_out, multiplexer_2_out, sub_1_s;
  wire [63:32] mul_1_mul;

  and and_1 (and_1_out, A[31], As);
  and and_2 (and_2_out, B[31], Bs);
  Mul #(.Bits(32)) mul_1 (.a(A), .b(B), .mul({mul_1_mul, L}));
  Multiplexer #(.Bits(32)) multiplexer_1 (.sel(and_1_out), .in_0({32{1'b0}}), .in_1(B), .out(multiplexer_1_out));
  Multiplexer #(.Bits(32)) multiplexer_2 (.sel(and_2_out), .in_0({32{1'b0}}), .in_1(A), .out(multiplexer_2_out));
  Sub #(.Bits(32)) sub_1 (.a(mul_1_mul), .b(multiplexer_1_out), .c_i(1'b0), .s(sub_1_s));  // open: c_o
  Sub #(.Bits(32)) sub_2 (.a(sub_1_s), .b(multiplexer_2_out), .c_i(1'b0), .s(H));  // open: c_o
endmodule
