// Digital circuit seq_div.dig as structural Verilog
module seq_div (
  input  clock,
  input  div,
  input  [31:0] A,
  input  [31:0] B,
  output stall,
  output [31:0] q,
  output [31:0] rem
);

  wire divstage_1_p3, nand_1_out;
  wire [3:0] counter_1_out;
  wire [31:0] divstage_2_p3, multiplexer_1_out, sll_1_out;
  wire [31:30] register_2_q;

  and and_1 (stall, nand_1_out, div);
  Counter #(.Bits(4)) counter_1 (.en(div), .C(clock), .clr(1'b0), .out(counter_1_out));  // open: ovf
  nand nand_1 (nand_1_out, counter_1_out[3], counter_1_out[2], counter_1_out[1], counter_1_out[0]);
  SLL sll_1 (.in(A), .shift({counter_1_out, 1'b0}), .out(sll_1_out));
  // divstage divstage_1: pin names not known; wires that end beside it: B, sll_1_out[30], divstage_1_p3, rem, q[0]
  // divstage divstage_2: pin names not known; wires that end beside it: B, sll_1_out[31], divstage_2_p3, divstage_1_p3, q[1]
  Register #(.Bits(32)) register_1 (.D(multiplexer_1_out), .C(clock), .en(div), .Q(divstage_2_p3));
  Multiplexer #(.Bits(32)) multiplexer_1 (.sel(stall), .in_0({32{1'b0}}), .in_1(rem), .out(multiplexer_1_out));
  Register #(.Bits(32)) register_2 (.D(q), .C(clock), .en(div), .Q({register_2_q, q[31:2]}));
endmodule
